// Logisim project DECA project.circ as structural Verilog: 1 circuit, main circuit main
module main (
  input  in_1,
  input  in_2,
  input  in_3,
  input  in_4,
  input  in_5,
  input  in_6,
  input  in_7,
  input  in_8
);

  wire and_1_out, and_2_out, and_3_out, and_4_out, and_5_out, and_6_out, and_7_out, and_8_out, and_9_out,
       and_10_out, and_11_out, and_12_out, and_13_out, and_14_out, and_15_out, and_16_out, and_17_out,
       and_18_out, and_19_out, and_20_out, and_21_out, clock_1_out, counter_1_carry, not_1_out, not_2_out,
       not_3_out, not_4_out, not_5_out, not_6_out, not_7_out, not_8_out, not_9_out, or_1_out, or_2_out,
       or_3_out, or_4_out, or_5_out, or_6_out, or_7_out, or_8_out, or_9_out, or_10_out, or_11_out, or_12_out,
       shift_register_1_out, shift_register_2_q0, shift_register_2_q1, shift_register_2_q2,
       shift_register_2_q3, shift_register_2_q4, xor_1_out;

  not not_1 (not_1_out, in_3);
  not not_2 (not_2_out, in_4);
  not not_3 (not_3_out, in_6);
  xor xor_1 (xor_1_out, in_4, in_5);
  and and_1 (and_1_out, not_1_out, not_2_out, in_6);
  or or_1 (or_1_out, xor_1_out, and_1_out);
  not not_4 (not_4_out, counter_1_carry);
  and and_2 (and_2_out, in_5, not_3_out);
  or or_2 (or_2_out, xor_1_out, and_2_out);
  Clock clock_1 (.out(clock_1_out));
  and and_3 (and_3_out, in_5, in_6);
  or or_3 (or_3_out, in_4, and_3_out);
  Shift_Register #(.length(5)) shift_register_1 (
    .shift(not_4_out), .in(in_7), .clk(clock_1_out), .out(shift_register_1_out), .load(counter_1_carry),
    .d0(or_1_out), .d1(or_2_out), .d2(or_3_out), .d3(or_4_out), .d4(or_5_out));  // open: clr, q0, q1, q2, q3, q4
  and and_4 (and_4_out, in_4, in_5);
  and and_5 (and_5_out, in_3, not_3_out);
  or or_4 (or_4_out, in_4, and_5_out);
  and and_6 (and_6_out, in_4, in_6);
  or or_5 (or_5_out, and_4_out, in_3, and_6_out);
  Counter #(.width(3), .max('h5)) counter_1 (
    .count(in_8), .carry(counter_1_carry), .clk(clock_1_out));  // open: load, D, Q, clr
  _7_Segment_Display u_7_segment_display_1 (.d(not_5_out), .dp(and_7_out));  // open: g, f, a, b, e, c
  and and_7 (and_7_out, counter_1_carry, shift_register_2_q0);
  and and_8 (and_8_out, counter_1_carry, shift_register_2_q1);
  and and_9 (and_9_out, counter_1_carry, shift_register_2_q2);
  and and_10 (and_10_out, counter_1_carry, shift_register_2_q3);
  and and_11 (and_11_out, counter_1_carry, shift_register_2_q4);
  _7_Segment_Display u_7_segment_display_2 (.d(not_8_out), .dp(and_9_out));  // open: g, f, a, b, e, c
  _7_Segment_Display u_7_segment_display_3 (.d(not_7_out), .dp(and_8_out));  // open: g, f, a, b, e, c
  _7_Segment_Display u_7_segment_display_4 (.d(not_6_out), .dp(and_10_out));  // open: g, f, a, b, e, c
  _7_Segment_Display u_7_segment_display_5 (.d(not_9_out), .dp(and_11_out));  // open: g, f, a, b, e, c
  Shift_Register #(.length(5)) shift_register_2 (
    .shift(in_2), .in(shift_register_1_out), .clk(clock_1_out), .load(in_1), .q0(shift_register_2_q0),
    .q1(shift_register_2_q1), .q2(shift_register_2_q2), .q3(shift_register_2_q3), .q4(shift_register_2_q4));  // open: out, clr, d0, d1, d2, d3, d4
  not not_5 (not_5_out, and_7_out);
  not not_6 (not_6_out, and_10_out);
  not not_7 (not_7_out, and_8_out);
  not not_8 (not_8_out, and_9_out);
  not not_9 (not_9_out, and_11_out);
  and and_12 (and_12_out, and_8_out, not_6_out);
  and and_13 (and_13_out, not_5_out, not_8_out);
  and and_14 (and_14_out, and_8_out, not_6_out);
  and and_15 (and_15_out, and_8_out, and_11_out);
  and and_16 (and_16_out, not_5_out, not_9_out);
  and and_17 (and_17_out, not_8_out, and_10_out);
  and and_18 (and_18_out, not_5_out, and_8_out);
  and and_19 (and_19_out, and_8_out, not_8_out);
  and and_20 (and_20_out, and_8_out, and_10_out);
  and and_21 (and_21_out, and_11_out, not_8_out);
  or or_6 (or_6_out, not_5_out, and_12_out, and_11_out);
  or or_7 (or_7_out, not_7_out, not_9_out);
  or or_8 (or_8_out, not_7_out, and_9_out);
  or or_9 (or_9_out, and_13_out, and_14_out, and_15_out);
  or or_10 (or_10_out, and_16_out, and_17_out, and_18_out, and_19_out);
  or or_11 (or_11_out, and_13_out, and_20_out);
  or or_12 (or_12_out, and_8_out, and_21_out);
  _7_Segment_Display u_7_segment_display_6 (
    .g(or_12_out), .f(or_11_out), .a(or_6_out), .b(or_7_out), .e(or_10_out), .d(or_9_out), .c(or_8_out));  // open: dp
endmodule
